// Logisim project AB_SAP1.circ as structural Verilog: 10 circuits, main circuit main
module main (
  input  EB,
  output CLK,
  output CLR,
  output EP,
  output CP,
  output LM,
  output EI,
  output CE,
  output LI,
  output EU,
  output SU,
  output LB,
  output LA,
  output EA,
  output CLR_2,
  output CLK_2,
  output [3:0] HIGH_4_7,
  output [3:0] LOW_0_3,
  output [11:0] out_19
);

  wire controlled_buffer_1_out, not_1_out;
  wire [3:0] MAR_q, OUT_output0x3, OUT_output4x7, PC_q;
  wire [7:0] IR_q, REG_A_directoutput, REG_B_directoutput;

  not not_1 (not_1_out, CLK);
  assign controlled_buffer_1_out = CP ? not_1_out : 1'bz;  // Controlled_Buffer controlled_buffer_1
  Register #(.width(4)) MAR (.D(LOW_0_3), .en(LM), .Q(MAR_q), .clk(CLK), .clr(CLR));
  Register IR (.D({HIGH_4_7, LOW_0_3}), .en(LI), .Q(IR_q), .clk(CLK), .clr(CLR));
  static_controller static_controller_1 (
    .CLK(CLK), .CLR(CLR), .INSTR(IR_q[7:4]),
    .MICROINSTRUCTION({CP, EP, LM, CE, LI, EI, LA, EA, out_19[3], EU, LB, out_19[0]}));
  assign LOW_0_3 = EP ? PC_q : 4'bz;  // Controlled_Buffer controlled_buffer_2
  Counter #(.width(4), .max('hf)) PC (
    .Q(PC_q), .clk(controlled_buffer_1_out), .clr(CLR));  // open: load, D, count, carry
  assign LOW_0_3 = EI ? IR_q[3:0] : 4'bz;  // Controlled_Buffer controlled_buffer_3
  RAM #(.addrWidth(4)) ram_1 (.addr(MAR_q), .data({HIGH_4_7, LOW_0_3}), .ld(CE));  // open: sel, clk, clr
  Register4x4 REG_A (
    .Output0x3(LOW_0_3), .Output4x7(HIGH_4_7), .Input0x3(LOW_0_3), .Input4x7(HIGH_4_7),
    .DirectOutput(REG_A_directoutput), .EnableOutput(EA), .CLR(CLR), .CLK(CLK), .LOAD(LA));
  ALU ALU (
    .Output0x3(LOW_0_3), .Output4x7(HIGH_4_7), .A(REG_A_directoutput), .B(REG_B_directoutput),
    .EnableOutput(EU), .Operation(out_19[3]));
  Register4x4 REG_B (
    .Output0x3(LOW_0_3), .Output4x7(HIGH_4_7), .Input0x3(LOW_0_3), .Input4x7(HIGH_4_7),
    .DirectOutput(REG_B_directoutput), .EnableOutput(EB), .CLR(CLR), .CLK(CLK), .LOAD(LB));
  Register4x4 OUT (
    .Output0x3(OUT_output0x3), .Output4x7(OUT_output4x7), .Input0x3(LOW_0_3), .Input4x7(HIGH_4_7),
    .EnableOutput(1'b1), .CLR(CLR), .CLK(CLK), .LOAD(out_19[0]));  // open: DirectOutput
  Clock clock_1 (.out(CLK));
  Button RST (.out(CLR));
  Hex_Digit_Display hex_digit_display_1 (.value(OUT_output4x7));  // open: dp
  Hex_Digit_Display hex_digit_display_2 (.value(OUT_output0x3));  // open: dp

  assign CLK_2 = CLK;
  assign CLR_2 = CLR;
  assign {out_19[11:4], out_19[2:1]} = {CP, EP, LM, CE, LI, EI, LA, EA, EU, LB};
  assign SU = out_19[3];

  // Notes on the sheet:
  //   RAM
  //   BUS
  //   Control wires
  //   EI -- enable IR
  //   Commands
  //   LDA 3
  //   ADD 4
  //   OUT
  //   CP -- increment PC
  //   EP - enable PC
  //   LM -- read RAM address
  //   CE -- output memory
  //   LI -- load instruction to IR
  //   LA -- load accumulator (reg A)
  //   EA -- enable accumulator
  //   SU -- subtraction
  //   EU -- enable ALU
  //   LB -- load reg B
  //   LO -- load output register
  //   0000 ADDR -- LDA ADDR
  //   0001 ADDR -- ADD ADDR
  //   0010 ADDR -- SUB ADDR
  //   1110            -- OUT
  //   Sample program
  //   03 14 e0 01 02
  //   1+2
endmodule

module Register4x4 (
  input  EnableOutput,
  input  CLR,
  input  [3:0] Input0x3,
  input  CLK,
  input  LOAD,
  input  [3:0] Input4x7,
  output [7:0] DirectOutput,
  output [3:0] Output0x3,
  output [3:0] Output4x7
);

  assign {Output4x7, Output0x3} = EnableOutput ? DirectOutput : 8'bz;  // Controlled_Buffer controlled_buffer_1
  Register Register (.D({Input4x7, Input0x3}), .en(LOAD), .Q(DirectOutput), .clk(CLK), .clr(CLR));
endmodule

module ALU (
  input  EnableOutput,
  input  [7:0] A,
  input  Operation,
  input  [7:0] B,
  output [3:0] Output0x3,
  output [3:0] Output4x7
);

  wire [7:0] adder_1_out, multiplexer_1_out, subtractor_1_out;

  assign {Output4x7, Output0x3} = EnableOutput ? multiplexer_1_out : 8'bz;  // Controlled_Buffer controlled_buffer_1
  Adder adder_1 (.a(A), .b(B), .out(adder_1_out));  // open: cin, cout
  Subtractor subtractor_1 (.a(A), .b(B), .out(subtractor_1_out));  // open: bin, bout
  Multiplexer #(.width(8), .enable("false")) multiplexer_1 (
    .in0(adder_1_out), .in1(subtractor_1_out), .out(multiplexer_1_out), .sel(Operation));
endmodule

module ring_counter_6 (
  input  CLK,
  input  CLR,
  output T1,
  output T2,
  output T3,
  output T4,
  output T5,
  output T6,
  output T7
);

  wire and_1_out, not_1_out, or_1_out, or_2_out;
  wire [3:0] counter_1_q;

  or or_1 (or_1_out, CLK, or_2_out);
  Counter #(.width(4), .max('hf)) counter_1 (
    .count(CLK), .Q(counter_1_q), .clk(or_1_out), .clr(or_2_out));  // open: load, D, carry
  not not_1 (not_1_out, counter_1_q[3]);
  or or_2 (or_2_out, CLR, and_1_out);
  and and_1 (and_1_out, not_1_out, counter_1_q[2], counter_1_q[1], counter_1_q[0]);
  Decoder #(.select(4)) decoder_1 (
    .out0(T1), .out1(T2), .out2(T3), .out3(T4), .out4(T5), .out5(T6), .out6(T7), .sel(counter_1_q));  // open: out7, out8, out9, out10, out11, out12, out13, out14, out15, en
endmodule

module static_controller (
  input  CLK,
  input  CLR,
  input  [3:0] INSTR,
  output [11:0] MICROINSTRUCTION
);

  wire and_6_out, and_8_out, and_9_out, and_10_out, instr_decoder_1_add, instr_decoder_1_lda,
       instr_decoder_1_out, instr_decoder_1_sub, or_1_out, or_2_out, ring_counter_6_1_t4,
       ring_counter_6_1_t5, ring_counter_6_1_t6, ring_counter_6_1_t7;

  instr_decoder instr_decoder_1 (
    .INSTR(INSTR), .LDA(instr_decoder_1_lda), .ADD(instr_decoder_1_add), .SUB(instr_decoder_1_sub),
    .OUT(instr_decoder_1_out));
  ring_counter_6 ring_counter_6_1 (
    .CLK(CLK), .CLR(CLR), .T1(MICROINSTRUCTION[10]), .T2(MICROINSTRUCTION[11]), .T3(MICROINSTRUCTION[7]),
    .T4(ring_counter_6_1_t4), .T5(ring_counter_6_1_t5), .T6(ring_counter_6_1_t6), .T7(ring_counter_6_1_t7));
  or or_1 (or_1_out, instr_decoder_1_sub, instr_decoder_1_add, instr_decoder_1_lda);
  or or_2 (or_2_out, instr_decoder_1_add, instr_decoder_1_sub);
  and and_1 (MICROINSTRUCTION[0], instr_decoder_1_out, ring_counter_6_1_t4);
  and and_2 (MICROINSTRUCTION[1], or_2_out, ring_counter_6_1_t5);
  and and_3 (MICROINSTRUCTION[2], ring_counter_6_1_t6, or_2_out);
  and and_4 (MICROINSTRUCTION[3], ring_counter_6_1_t6, instr_decoder_1_sub);
  and and_5 (MICROINSTRUCTION[4], instr_decoder_1_out, ring_counter_6_1_t4);
  and and_6 (and_6_out, or_2_out, ring_counter_6_1_t6);
  or or_3 (MICROINSTRUCTION[5], and_6_out, and_8_out);
  and and_7 (MICROINSTRUCTION[6], or_1_out, ring_counter_6_1_t4);
  and and_8 (and_8_out, instr_decoder_1_lda, ring_counter_6_1_t5);
  and and_9 (and_9_out, or_1_out, ring_counter_6_1_t5);
  or or_4 (MICROINSTRUCTION[8], and_9_out, MICROINSTRUCTION[7]);
  and and_10 (and_10_out, or_1_out, ring_counter_6_1_t4);
  or or_5 (MICROINSTRUCTION[9], and_10_out, MICROINSTRUCTION[10]);
  Hex_Digit_Display hex_digit_display_1 (.value(MICROINSTRUCTION[11:8]));  // open: dp
  Hex_Digit_Display hex_digit_display_2 (.value(MICROINSTRUCTION[3:0]));  // open: dp
  Hex_Digit_Display hex_digit_display_3 (.value(MICROINSTRUCTION[7:4]));  // open: dp

  // Notes on the sheet:
  //   LDA
  //   ADD
  //   SUB
  //   OUT
endmodule

module instr_decoder (
  input  [3:0] INSTR,
  output LDA,
  output ADD,
  output SUB,
  output OUT
);

  wire [3:0] not_1_out;

  assign not_1_out = ~INSTR;  // NOT_Gate not_1, 4 bits wide
  and and_1 (LDA, not_1_out[3], not_1_out[2], not_1_out[1], not_1_out[0]);
  and and_2 (ADD, not_1_out[3], not_1_out[2], not_1_out[1], INSTR[0]);
  and and_3 (SUB, not_1_out[3], not_1_out[2], INSTR[1], not_1_out[0]);
  and and_4 (OUT, INSTR[3], INSTR[2], INSTR[1], not_1_out[0]);
endmodule

module main____rom_programming (
  input  EB,
  output CLK,
  output CLR,
  output EP,
  output CP,
  output LM,
  output EI,
  output CE,
  output LI,
  output EU,
  output SU,
  output LB,
  output LA,
  output EA,
  output CLR_2,
  output CLK_2,
  output [3:0] HIGH_4_7,
  output [3:0] LOW_0_3,
  output [3:0] out_19,
  output [11:0] out_20
);

  wire controlled_buffer_1_out, not_1_out, rom_controller_1_ce, rom_controller_1_cp, rom_controller_1_eu;
  wire [3:0] IR_q, MAR_q, OUT_output0x3, OUT_output4x7, PC_q;
  wire [7:0] REG_A_directoutput, REG_B_directoutput;

  not not_1 (not_1_out, CLK);
  assign controlled_buffer_1_out = CP ? not_1_out : 1'bz;  // Controlled_Buffer controlled_buffer_1
  Register #(.width(4)) MAR (.D(LOW_0_3), .en(LM), .Q(MAR_q), .clk(CLK), .clr(CLR));
  Register IR (.D({HIGH_4_7, LOW_0_3}), .en(LI), .Q({out_19, IR_q}), .clk(CLK), .clr(CLR));
  rom_controller rom_controller_1 (
    .CMD(out_19), .CLK(CLK), .RST(CLR), .CP(rom_controller_1_cp), .EP(rom_controller_1_cp),
    .CE(rom_controller_1_ce), .LI(rom_controller_1_ce), .EU(rom_controller_1_eu), .LB(rom_controller_1_eu),
    .LO(rom_controller_1_eu), .out_4({CP, EP, LM, CE, LI, EI, LA, EA, out_20[3], EU, LB, out_20[0]}));  // open: LM, EI, LA, EA, SU
  assign LOW_0_3 = EP ? PC_q : 4'bz;  // Controlled_Buffer controlled_buffer_2
  Counter #(.width(4), .max('hf)) PC (
    .Q(PC_q), .clk(controlled_buffer_1_out), .clr(CLR));  // open: load, D, count, carry
  assign LOW_0_3 = EI ? IR_q : 4'bz;  // Controlled_Buffer controlled_buffer_3
  RAM #(.addrWidth(4)) ram_1 (.addr(MAR_q), .data({HIGH_4_7, LOW_0_3}), .ld(CE));  // open: sel, clk, clr
  Register4x4 REG_A (
    .Output0x3(LOW_0_3), .Output4x7(HIGH_4_7), .Input0x3(LOW_0_3), .Input4x7(HIGH_4_7),
    .DirectOutput(REG_A_directoutput), .EnableOutput(EA), .CLR(CLR), .CLK(CLK), .LOAD(LA));
  ALU ALU (
    .Output0x3(LOW_0_3), .Output4x7(HIGH_4_7), .A(REG_A_directoutput), .B(REG_B_directoutput),
    .EnableOutput(EU), .Operation(out_20[3]));
  Register4x4 REG_B (
    .Output0x3(LOW_0_3), .Output4x7(HIGH_4_7), .Input0x3(LOW_0_3), .Input4x7(HIGH_4_7),
    .DirectOutput(REG_B_directoutput), .EnableOutput(EB), .CLR(CLR), .CLK(CLK), .LOAD(LB));
  Register4x4 OUT (
    .Output0x3(OUT_output0x3), .Output4x7(OUT_output4x7), .Input0x3(LOW_0_3), .Input4x7(HIGH_4_7),
    .EnableOutput(1'b1), .CLR(CLR), .CLK(CLK), .LOAD(out_20[0]));  // open: DirectOutput
  Clock clock_1 (.out(CLK));
  Button RST (.out(CLR));
  Hex_Digit_Display hex_digit_display_1 (.value(OUT_output0x3));  // open: dp
  Hex_Digit_Display hex_digit_display_2 (.value(OUT_output4x7));  // open: dp

  assign CLK_2 = CLK;
  assign CLR_2 = CLR;
  assign {out_20[11:4], out_20[2:1]} = {CP, EP, LM, CE, LI, EI, LA, EA, EU, LB};
  assign SU = out_20[3];

  // Notes on the sheet:
  //   RAM
  //   BUS
  //   Control wires
  //   EI -- enable IR
  //   Commands
  //   LDA 3
  //   ADD 4
  //   OUT
  //   CP -- increment PC
  //   EP - enable PC
  //   LM -- read RAM address
  //   CE -- output memory
  //   LI -- load instruction to IR
  //   LA -- load accumulator (reg A)
  //   EA -- enable accumulator
  //   SU -- subtraction
  //   EU -- enable ALU
  //   LB -- load reg B
  //   LO -- load output register
  //   0000 ADDR -- LDA ADDR
  //   0001 ADDR -- ADD ADDR
  //   0010 ADDR -- SUB ADDR
  //   1110            -- OUT
  //   Sample program
  //   03 14 e0 01 02
  //   1+2
endmodule

module timer (
  input  CLK,
  input  CLR,
  output T1,
  output T3,
  output T4
);

  wire and_1_out, not_1_out, or_1_out;
  wire [2:0] counter_1_q;

  Decoder #(.select(3)) decoder_1 (
    .out0(T1), .out2(T3), .out3(T4), .sel(counter_1_q));  // open: out1, out4, out5, out6, out7, en
  Counter #(.width(3), .max('h6)) counter_1 (
    .Q(counter_1_q), .clk(CLK), .clr(or_1_out));  // open: load, D, count, carry
  not not_1 (not_1_out, counter_1_q[0]);
  and and_1 (and_1_out, not_1_out, counter_1_q[1], counter_1_q[2]);
  or or_1 (or_1_out, and_1_out, CLR);
endmodule

module preset_counter (
  input  RST,
  input  CLK,
  input  LOAD,
  input  [3:0] DI,
  output [3:0] Q
);

  wire and_1_out, and_2_out, and_3_out, and_4_out, and_5_out, and_6_out, and_7_out, and_8_out, and_9_out,
       and_10_out, not_1_out, not_2_out, not_3_out, not_4_out, not_5_out, or_1_out, or_2_out, or_3_out,
       or_4_out, undriven, undriven_2, undriven_3, undriven_4, undriven_5, undriven_6, undriven_7, undriven_8;

  not not_1 (not_1_out, CLK);
  and and_1 (and_1_out, LOAD, undriven, DI[0]);
  J_K_Flip_Flop j_k_ff_1 (
    .J(1'b1), .clk(not_1_out), .K(1'b1), .Q(Q[0]), .preset(and_1_out), .reset(or_1_out));  // open: Qn, en
  or or_1 (or_1_out, RST, and_2_out);
  and and_2 (and_2_out, LOAD, undriven_2, not_2_out);
  not not_2 (not_2_out, DI[0]);
  J_K_Flip_Flop j_k_ff_2 (
    .J(Q[0]), .clk(not_1_out), .K(Q[0]), .Q(Q[1]), .preset(and_3_out), .reset(or_2_out));  // open: Qn, en
  or or_2 (or_2_out, RST, and_5_out);
  and and_3 (and_3_out, LOAD, undriven_3, DI[1]);
  and and_4 (and_4_out, Q[0], Q[1]);
  and and_5 (and_5_out, LOAD, undriven_4, not_3_out);
  not not_3 (not_3_out, DI[1]);
  and and_6 (and_6_out, LOAD, undriven_5, DI[2]);
  and and_7 (and_7_out, and_4_out, Q[2]);
  J_K_Flip_Flop j_k_ff_3 (
    .J(and_4_out), .clk(not_1_out), .K(and_4_out), .Q(Q[2]), .preset(and_6_out), .reset(or_3_out));  // open: Qn, en
  or or_3 (or_3_out, RST, and_8_out);
  and and_8 (and_8_out, LOAD, undriven_6, not_4_out);
  not not_4 (not_4_out, DI[2]);
  and and_9 (and_9_out, LOAD, undriven_7, DI[3]);
  J_K_Flip_Flop j_k_ff_4 (
    .J(and_7_out), .clk(not_1_out), .K(and_7_out), .Q(Q[3]), .preset(and_9_out), .reset(or_4_out));  // open: Qn, en
  or or_4 (or_4_out, RST, and_10_out);
  and and_10 (and_10_out, LOAD, undriven_8, not_5_out);
  not not_5 (not_5_out, DI[3]);
endmodule

module rom_controller (
  input  [3:0] CMD,
  input  CLK,
  input  RST,
  output [11:0] out_4,
  output CP,
  output EP,
  output LM,
  output CE,
  output LI,
  output EI,
  output LA,
  output EA,
  output SU,
  output EU,
  output LB,
  output LO
);

  wire decoder_1_out6, or_1_out;
  wire [2:0] counter_1_q;

  LED led_1 (.in(counter_1_q[1]));
  LED led_2 (.in(counter_1_q[2]));
  LED led_3 (.in(counter_1_q[0]));
  Counter #(.width(3), .max('h7), .ongoal("continue"), .trigger("falling")) counter_1 (
    .count(1'b1), .Q(counter_1_q), .clk(CLK), .clr(or_1_out));  // open: load, D, carry
  Decoder #(.select(3)) decoder_1 (
    .out6(decoder_1_out6), .sel(counter_1_q), .en(1'b1));  // open: out0, out1, out2, out3, out4, out5, out7
  or or_1 (or_1_out, RST, decoder_1_out6);
  ROM #(.addrWidth(7), .dataWidth(12)) rom_1 (
    .addr({CMD, counter_1_q}), .data({CP, EP, LM, CE, LI, EI, LA, EA, out_4[3], EU, LB, LO}), .sel(1'b1));

  assign {out_4[11:4], out_4[2:0]} = {CP, EP, LM, CE, LI, EI, LA, EA, EU, LB, LO};
  assign SU = out_4[3];

  // Notes on the sheet:
  //   Microcode Counter
  //   contents of rom_1 (hex, n*v repeats v):
  //   600 800 180 240 120 0 0 0 600 800 180 240 102 24 0 0 600 800 180 240 102 2c 36*0 100 53*0 600 800
  //   180 11
endmodule
