// Logisim project AB_SAP_ROM.circ as structural Verilog: 11 circuits, main circuit main
module main (
  input  EB,
  output CLK,
  output CLR,
  output EP,
  output CP,
  output LM,
  output EI,
  output CE,
  output LI,
  output EU,
  output SU,
  output LB,
  output LA,
  output EA,
  output CLR_2,
  output CLK_2,
  output [3:0] HIGH_4_7,
  output [3:0] LOW_0_3,
  output [11:0] out_19
);

  wire controlled_buffer_1_out, not_1_out;
  wire [3:0] MAR_q, OUT_output0x3, OUT_output4x7, PC_q;
  wire [7:0] IR_q, REG_A_directoutput, REG_B_directoutput;

  not not_1 (not_1_out, CLK);
  assign controlled_buffer_1_out = CP ? not_1_out : 1'bz;  // Controlled_Buffer controlled_buffer_1
  Register #(.width(4)) MAR (.D(LOW_0_3), .en(LM), .Q(MAR_q), .clk(CLK), .clr(CLR));
  Register IR (.D({HIGH_4_7, LOW_0_3}), .en(LI), .Q(IR_q), .clk(CLK), .clr(CLR));
  static_controller static_controller_1 (
    .CLK(CLK), .CLR(CLR), .INSTR(IR_q[7:4]),
    .MICROINSTRUCTION({CP, EP, LM, CE, LI, EI, LA, EA, out_19[3], EU, LB, out_19[0]}));
  Counter #(.width(4), .max('hf)) PC (
    .Q(PC_q), .clk(controlled_buffer_1_out), .clr(CLR));  // open: load, D, count, carry
  assign LOW_0_3 = EP ? PC_q : 4'bz;  // Controlled_Buffer controlled_buffer_2
  assign LOW_0_3 = EI ? IR_q[3:0] : 4'bz;  // Controlled_Buffer controlled_buffer_3
  RAM #(.addrWidth(4)) ram_1 (.addr(MAR_q), .data({HIGH_4_7, LOW_0_3}), .ld(CE));  // open: sel, clk, clr
  Register4x4 REG_A (
    .Output0x3(LOW_0_3), .Output4x7(HIGH_4_7), .Input0x3(LOW_0_3), .Input4x7(HIGH_4_7), .EnableOutput(EA),
    .CLR(CLR), .CLK(CLK), .LOAD(LA), .DirectOutput(REG_A_directoutput));
  ALU ALU (
    .Output0x3(LOW_0_3), .Output4x7(HIGH_4_7), .A(REG_A_directoutput), .B(REG_B_directoutput),
    .EnableOutput(EU), .Operation_low(out_19[3]));  // open: Operation
  Register4x4 REG_B (
    .Output0x3(LOW_0_3), .Output4x7(HIGH_4_7), .Input0x3(LOW_0_3), .Input4x7(HIGH_4_7), .EnableOutput(EB),
    .CLR(CLR), .CLK(CLK), .LOAD(LB), .DirectOutput(REG_B_directoutput));
  Register4x4 OUT (
    .Output0x3(OUT_output0x3), .Output4x7(OUT_output4x7), .Input0x3(LOW_0_3), .Input4x7(HIGH_4_7),
    .EnableOutput(1'b1), .CLR(CLR), .CLK(CLK), .LOAD(out_19[0]));  // open: DirectOutput
  Clock clock_1 (.out(CLK));
  Button RST (.out(CLR));
  Hex_Digit_Display hex_digit_display_1 (.value(OUT_output4x7));  // open: dp
  Hex_Digit_Display hex_digit_display_2 (.value(OUT_output0x3));  // open: dp

  assign CLK_2 = CLK;
  assign CLR_2 = CLR;
  assign {out_19[11:4], out_19[2:1]} = {CP, EP, LM, CE, LI, EI, LA, EA, EU, LB};
  assign SU = out_19[3];

  // Notes on the sheet:
  //   RAM
  //   BUS
  //   Control wires
  //   EI -- enable IR
  //   Commands
  //   LDA 3
  //   ADD 4
  //   OUT
  //   CP -- increment PC
  //   EP - enable PC
  //   LM -- read RAM address
  //   CE -- output memory
  //   LI -- load instruction to IR
  //   LA -- load accumulator (reg A)
  //   EA -- enable accumulator
  //   SU -- subtraction
  //   EU -- enable ALU
  //   LB -- load reg B
  //   LO -- load output register
  //   0000 ADDR -- LDA ADDR
  //   0001 ADDR -- ADD ADDR
  //   0010 ADDR -- SUB ADDR
  //   1110            -- OUT
  //   Sample program
  //   03 14 e0 01 02
  //   1+2
endmodule

module Register4x4 (
  input  EnableOutput,
  input  CLR,
  input  [3:0] Input0x3,
  input  CLK,
  input  LOAD,
  input  [3:0] Input4x7,
  output [7:0] DirectOutput,
  output [3:0] Output0x3,
  output [3:0] Output4x7
);

  assign {Output4x7, Output0x3} = EnableOutput ? DirectOutput : 8'bz;  // Controlled_Buffer controlled_buffer_1
  Register Register (.D({Input4x7, Input0x3}), .en(LOAD), .Q(DirectOutput), .clk(CLK), .clr(CLR));
endmodule

module ALU (
  input  EnableOutput,
  input  [7:0] A,
  input  [1:0] Operation,
  input  [7:0] B,
  input  Operation_low,
  output [3:0] Output0x3,
  output [3:0] Output4x7
);

  wire [7:0] adder_1_out, divider_1_out, multiplexer_1_out, multiplier_1_out, subtractor_1_out;

  assign {Output4x7, Output0x3} = EnableOutput ? multiplexer_1_out : 8'bz;  // Controlled_Buffer controlled_buffer_1
  Adder adder_1 (.a(A), .b(B), .out(adder_1_out));  // open: cin, cout
  Subtractor subtractor_1 (.a(A), .b(B), .out(subtractor_1_out));  // open: bin, bout
  Multiplier multiplier_1 (.a(A), .b(B), .out(multiplier_1_out));  // open: cin, cout
  Divider divider_1 (.a(A), .b(B), .out(divider_1_out));  // open: upper, rem
  Multiplexer #(.select(2), .width(8), .enable("false")) multiplexer_1 (
    .in0(adder_1_out), .in1(subtractor_1_out), .in2(multiplier_1_out), .in3(divider_1_out),
    .out(multiplexer_1_out), .sel(Operation));

  assign Operation_low = Operation[0];
endmodule

module ring_counter_6 (
  input  CLK,
  input  CLR,
  output T1,
  output T2,
  output T3,
  output T4,
  output T5,
  output T6,
  output T7
);

  wire and_1_out, not_1_out, or_1_out, or_2_out;
  wire [3:0] counter_1_q;

  or or_1 (or_1_out, CLK, or_2_out);
  Counter #(.width(4), .max('hf)) counter_1 (
    .count(CLK), .Q(counter_1_q), .clk(or_1_out), .clr(or_2_out));  // open: load, D, carry
  not not_1 (not_1_out, counter_1_q[3]);
  or or_2 (or_2_out, CLR, and_1_out);
  and and_1 (and_1_out, not_1_out, counter_1_q[2], counter_1_q[1], counter_1_q[0]);
  Decoder #(.select(4)) decoder_1 (
    .out0(T1), .out1(T2), .out2(T3), .out3(T4), .out4(T5), .out5(T6), .out6(T7), .sel(counter_1_q));  // open: out7, out8, out9, out10, out11, out12, out13, out14, out15, en
endmodule

module static_controller (
  input  CLK,
  input  CLR,
  input  [3:0] INSTR,
  output [11:0] MICROINSTRUCTION
);

  wire and_6_out, and_7_out, and_9_out, and_10_out, instr_decoder_1_add, instr_decoder_1_lda,
       instr_decoder_1_out, instr_decoder_1_sub, or_1_out, or_2_out, ring_counter_6_1_t4,
       ring_counter_6_1_t5, ring_counter_6_1_t6, ring_counter_6_1_t7;

  instr_decoder instr_decoder_1 (
    .INSTR(INSTR), .LDA(instr_decoder_1_lda), .ADD(instr_decoder_1_add), .SUB(instr_decoder_1_sub),
    .OUT(instr_decoder_1_out));
  ring_counter_6 ring_counter_6_1 (
    .CLK(CLK), .CLR(CLR), .T1(MICROINSTRUCTION[10]), .T2(MICROINSTRUCTION[11]), .T3(MICROINSTRUCTION[7]),
    .T4(ring_counter_6_1_t4), .T5(ring_counter_6_1_t5), .T6(ring_counter_6_1_t6), .T7(ring_counter_6_1_t7));
  or or_1 (or_1_out, instr_decoder_1_sub, instr_decoder_1_add, instr_decoder_1_lda);
  or or_2 (or_2_out, instr_decoder_1_add, instr_decoder_1_sub);
  and and_1 (MICROINSTRUCTION[0], instr_decoder_1_out, ring_counter_6_1_t4);
  and and_2 (MICROINSTRUCTION[1], or_2_out, ring_counter_6_1_t5);
  and and_3 (MICROINSTRUCTION[2], ring_counter_6_1_t6, or_2_out);
  and and_4 (MICROINSTRUCTION[3], ring_counter_6_1_t6, instr_decoder_1_sub);
  and and_5 (MICROINSTRUCTION[4], instr_decoder_1_out, ring_counter_6_1_t4);
  and and_6 (and_6_out, or_2_out, ring_counter_6_1_t6);
  or or_3 (MICROINSTRUCTION[5], and_6_out, and_7_out);
  and and_7 (and_7_out, instr_decoder_1_lda, ring_counter_6_1_t5);
  and and_8 (MICROINSTRUCTION[6], or_1_out, ring_counter_6_1_t4);
  and and_9 (and_9_out, or_1_out, ring_counter_6_1_t5);
  or or_4 (MICROINSTRUCTION[8], and_9_out, MICROINSTRUCTION[7]);
  and and_10 (and_10_out, or_1_out, ring_counter_6_1_t4);
  or or_5 (MICROINSTRUCTION[9], and_10_out, MICROINSTRUCTION[10]);
  Hex_Digit_Display hex_digit_display_1 (.value(MICROINSTRUCTION[11:8]));  // open: dp
  Hex_Digit_Display hex_digit_display_2 (.value(MICROINSTRUCTION[7:4]));  // open: dp
  Hex_Digit_Display hex_digit_display_3 (.value(MICROINSTRUCTION[3:0]));  // open: dp

  // Notes on the sheet:
  //   LDA
  //   ADD
  //   SUB
  //   OUT
endmodule

module instr_decoder (
  input  [3:0] INSTR,
  output LDA,
  output ADD,
  output SUB,
  output OUT
);

  wire [3:0] not_1_out;

  assign not_1_out = ~INSTR;  // NOT_Gate not_1, 4 bits wide
  and and_1 (LDA, not_1_out[3], not_1_out[2], not_1_out[1], not_1_out[0]);
  and and_2 (ADD, not_1_out[3], not_1_out[2], not_1_out[1], INSTR[0]);
  and and_3 (SUB, not_1_out[3], not_1_out[2], INSTR[1], not_1_out[0]);
  and and_4 (OUT, INSTR[3], INSTR[2], INSTR[1], not_1_out[0]);
endmodule

module main____rom_programming (
  output [3:0] HIGH_4_7,
  output [3:0] LOW_0_3,
  output [7:0] Register_A,
  output [7:0] out_4,
  output [7:0] out_5,
  output [3:0] out_6,
  output [7:0] Register_B
);

  wire CE, CLK, CLR, controlled_buffer_2_out, CP, EA, EI, EP, EU, LA, LB, LI, LM, LO, not_1_out, not_2_out,
       WM;
  wire [1:0] OP, rom_controller_1_out_4;
  wire [3:0] counter_q, IR_q, MAR_q;
  wire [7:0] controlled_buffer_1_out, OUT;

  assign controlled_buffer_1_out = WM ? {HIGH_4_7, LOW_0_3} : 8'bz;  // Controlled_Buffer controlled_buffer_1
  Register #(.width(4)) MAR (.D(LOW_0_3), .en(LM), .Q(MAR_q), .clk(CLK), .clr(CLR));
  not not_1 (not_1_out, CLK);
  assign controlled_buffer_2_out = CP ? not_1_out : 1'bz;  // Controlled_Buffer controlled_buffer_2
  not not_2 (not_2_out, WM);
  Register IR (.D({HIGH_4_7, LOW_0_3}), .en(LI), .Q({out_6, IR_q}), .clk(CLK), .clr(CLR));
  Counter #(.width(4), .max('hf)) counter (
    .Q(counter_q), .clk(controlled_buffer_2_out), .clr(CLR));  // open: load, D, count, carry
  assign LOW_0_3 = EP ? counter_q : 4'bz;  // Controlled_Buffer controlled_buffer_3
  RAM #(.addrWidth(4)) ram_1 (
    .addr(MAR_q), .data(controlled_buffer_1_out), .clk(CLK), .ld(not_2_out));  // open: sel, clr
  assign LOW_0_3 = EI ? IR_q : 4'bz;  // Controlled_Buffer controlled_buffer_4
  rom_controller rom_controller_1 (
    .INSTR(out_6), .CLK(CLK), .RST(CLR),
    .out_4({CP, EP, LM, CE, LI, EI, LA, EA, WM, EU, LB, LO, OP, rom_controller_1_out_4}));
  assign {HIGH_4_7, LOW_0_3} = CE ? controlled_buffer_1_out : 8'bz;  // Controlled_Buffer controlled_buffer_5
  Register4x4 REG_A (
    .Output0x3(LOW_0_3), .Output4x7(HIGH_4_7), .Input0x3(LOW_0_3), .Input4x7(HIGH_4_7), .EnableOutput(EA),
    .CLR(CLR), .CLK(CLK), .LOAD(LA), .DirectOutput(out_4));
  ALU alu_1 (
    .Output0x3(LOW_0_3), .Output4x7(HIGH_4_7), .A(out_4), .B(out_5), .EnableOutput(EU), .Operation(OP));  // open: Operation_low
  Register4x4 REG_B (
    .Output0x3(LOW_0_3), .Output4x7(HIGH_4_7), .Input0x3(LOW_0_3), .Input4x7(HIGH_4_7), .EnableOutput(1'b0),
    .CLR(CLR), .CLK(CLK), .LOAD(LB), .DirectOutput(out_5));
  Register4x4 u_OUT (
    .Output0x3(OUT[3:0]), .Output4x7(OUT[7:4]), .Input0x3(LOW_0_3), .Input4x7(HIGH_4_7), .EnableOutput(1'b1),
    .CLR(CLR), .CLK(CLK), .LOAD(LO));  // open: DirectOutput
  Clock clock_1 (.out(CLK));
  Button RST (.out(CLR));
  Hex_Digit_Display hex_digit_display_1 (.value(OUT[7:4]));  // open: dp
  Hex_Digit_Display hex_digit_display_2 (.value(OUT[3:0]));  // open: dp
  LED led_1 (.in(CP));
  LED led_2 (.in(EP));
  LED led_3 (.in(LM));
  LED led_4 (.in(CE));
  LED led_5 (.in(LI));
  LED led_6 (.in(EI));
  LED led_7 (.in(LA));
  LED led_8 (.in(EA));
  LED led_9 (.in(WM));
  LED led_10 (.in(EU));
  LED led_11 (.in(LB));
  LED led_12 (.in(LO));
  LED led_13 (.in(OP[1]));
  LED led_14 (.in(OP[0]));

  assign Register_A = out_4;
  assign Register_B = out_5;

  // Other names for the same wires on the sheet: INSTR[3:0] = out_6; RegA[7:0] = out_4; RegB[7:0] = out_5

  // Notes on the sheet:
  //   Program Counter (PC)
  //   Random Access Memory (RAM)
  //   Instruction Register (IR)
  //   Controller
  //   BUS
  //   Arithmetic Logic Unit (ALU)
  //   Output Register
  //   Control wires
  //   CP -- increment PC
  //   EP - enable PC
  //   LM -- read RAM address
  //   CE -- output memory
  //   LI -- load instruction to IR
  //   EI -- enable IR
  //   EA -- enable accumulator
  //   SU -- subtraction
  //   EU -- enable ALU
  //   LB -- load reg B
  //   LO -- load output register
  //   Commands
  //   0000 ADDR -- LDA ADDR
  //   0001 ADDR -- ADD ADDR
  //   0010 ADDR -- SUB ADDR
  //   1110            -- OUT
  //   Sample program
  //   04 35 e0 f0 02 03
  //   Input/Output Block
  //   LA -- load accumulator (reg A)
  //   2*3
endmodule

module timer (
  input  CLK,
  input  CLR,
  output T1,
  output T3,
  output T4
);

  wire and_1_out, not_1_out, or_1_out;
  wire [2:0] counter_1_q;

  Decoder #(.select(3)) decoder_1 (
    .out0(T1), .out2(T3), .out3(T4), .sel(counter_1_q));  // open: out1, out4, out5, out6, out7, en
  Counter #(.width(3), .max('h6)) counter_1 (
    .Q(counter_1_q), .clk(CLK), .clr(or_1_out));  // open: load, D, count, carry
  not not_1 (not_1_out, counter_1_q[0]);
  and and_1 (and_1_out, not_1_out, counter_1_q[1], counter_1_q[2]);
  or or_1 (or_1_out, and_1_out, CLR);
endmodule

module preset_counter (
  input  RST,
  input  CLK,
  input  LOAD,
  input  [3:0] DI,
  output [3:0] Q
);

  wire and_1_out, and_2_out, and_3_out, and_4_out, and_5_out, and_6_out, and_7_out, and_8_out, and_9_out,
       and_10_out, not_1_out, not_2_out, not_3_out, not_4_out, not_5_out, or_1_out, or_2_out, or_3_out,
       or_4_out, undriven, undriven_2, undriven_3, undriven_4, undriven_5, undriven_6, undriven_7, undriven_8;

  not not_1 (not_1_out, CLK);
  and and_1 (and_1_out, LOAD, undriven, DI[0]);
  J_K_Flip_Flop j_k_ff_1 (
    .J(1'b1), .clk(not_1_out), .K(1'b1), .Q(Q[0]), .preset(and_1_out), .reset(or_1_out));  // open: Qn, en
  or or_1 (or_1_out, RST, and_2_out);
  and and_2 (and_2_out, LOAD, undriven_2, not_2_out);
  not not_2 (not_2_out, DI[0]);
  J_K_Flip_Flop j_k_ff_2 (
    .J(Q[0]), .clk(not_1_out), .K(Q[0]), .Q(Q[1]), .preset(and_3_out), .reset(or_2_out));  // open: Qn, en
  or or_2 (or_2_out, RST, and_5_out);
  and and_3 (and_3_out, LOAD, undriven_3, DI[1]);
  and and_4 (and_4_out, Q[0], Q[1]);
  and and_5 (and_5_out, LOAD, undriven_4, not_3_out);
  not not_3 (not_3_out, DI[1]);
  and and_6 (and_6_out, LOAD, undriven_5, DI[2]);
  and and_7 (and_7_out, and_4_out, Q[2]);
  J_K_Flip_Flop j_k_ff_3 (
    .J(and_4_out), .clk(not_1_out), .K(and_4_out), .Q(Q[2]), .preset(and_6_out), .reset(or_3_out));  // open: Qn, en
  or or_3 (or_3_out, RST, and_8_out);
  and and_8 (and_8_out, LOAD, undriven_6, not_4_out);
  not not_4 (not_4_out, DI[2]);
  and and_9 (and_9_out, LOAD, undriven_7, DI[3]);
  J_K_Flip_Flop j_k_ff_4 (
    .J(and_7_out), .clk(not_1_out), .K(and_7_out), .Q(Q[3]), .preset(and_9_out), .reset(or_4_out));  // open: Qn, en
  or or_4 (or_4_out, RST, and_10_out);
  and and_10 (and_10_out, LOAD, undriven_8, not_5_out);
  not not_5 (not_5_out, DI[3]);
endmodule

module rom_controller (
  input  [3:0] INSTR,
  input  CLK,
  input  RST,
  output [15:0] out_4
);

  wire decoder_1_out6, or_1_out;
  wire [2:0] counter_1_q;

  LED CP (.in(out_4[15]));
  LED led_1 (.in(counter_1_q[1]));
  LED led_2 (.in(counter_1_q[0]));
  LED led_3 (.in(counter_1_q[2]));
  Counter #(.width(3), .max('h7), .ongoal("continue"), .trigger("falling")) counter_1 (
    .count(1'b1), .Q(counter_1_q), .clk(CLK), .clr(or_1_out));  // open: load, D, carry
  or or_1 (or_1_out, RST, decoder_1_out6);
  LED LM (.in(out_4[13]));
  LED EP (.in(out_4[14]));
  Decoder #(.select(3)) decoder_1 (
    .out6(decoder_1_out6), .sel(counter_1_q), .en(1'b1));  // open: out0, out1, out2, out3, out4, out5, out7
  LED CE (.in(out_4[12]));
  LED EI (.in(out_4[10]));
  LED LI (.in(out_4[11]));
  LED EA (.in(out_4[8]));
  LED LA (.in(out_4[9]));
  LED WM (.in(out_4[7]));
  ROM #(.addrWidth(7), .dataWidth(16)) rom_1 (.addr({INSTR, counter_1_q}), .data(out_4), .sel(1'b1));
  LED EU (.in(out_4[6]));
  LED LB (.in(out_4[5]));
  LED LO (.in(out_4[4]));
  LED OP1 (.in(out_4[3]));
  LED OP0 (.in(out_4[2]));
  LED RES (.in(out_4[0]));
  LED RES_2 (.in(out_4[1]));

  // Notes on the sheet:
  //   Microcode Counter
  //   contents of rom_1 (hex, n*v repeats v):
  //   6000 8000 1800 2400 1200 0 0 0 6000 8000 1800 2400 1020 240 0 0 6000 8000 1800 2400 1020 244 0 0
  //   6000 8000 1800 2400 1020 248 0 0 6000 8000 1800 2400 1020 24c 0 0 6000 8000 1800 2400 180 67*0 6000
  //   8000 1800 110
  //   1110            -- OUT
  //   0000 ADDR -- LDA ADDR
  //   0001 ADDR -- ADD ADDR
  //   0010 ADDR -- SUB ADDR
endmodule

module mem_exp (
  input  in_1,
  input  in_2,
  input  in_3,
  input  in_4,
  input  in_5
);

  wire not_1_out;
  wire [3:0] MAR_2_q, MAR_q, undriven, undriven_2;
  wire [7:0] controlled_buffer_1_out, controlled_buffer_2_out, ram_1_data;

  Register #(.width(4)) MAR (.D(undriven), .en(in_1), .Q(MAR_q), .clk(in_2), .clr(in_3));
  RAM #(.addrWidth(4)) ram_1 (.addr(MAR_q), .data(ram_1_data), .ld(in_4));  // open: sel, clk, clr
  assign controlled_buffer_1_out = in_5 ? controlled_buffer_2_out : 8'bz;  // Controlled_Buffer controlled_buffer_1
  Register #(.width(4)) MAR_2 (.D(undriven_2), .en(in_1), .Q(MAR_2_q), .clk(in_2), .clr(in_3));
  not not_1 (not_1_out, in_5);
  RAM #(.addrWidth(4)) ram_2 (
    .addr(MAR_2_q), .data(controlled_buffer_1_out), .clk(in_2), .ld(not_1_out));  // open: sel, clr
  assign controlled_buffer_2_out = in_4 ? controlled_buffer_1_out : 8'bz;  // Controlled_Buffer controlled_buffer_2

  // Other names for the same wires on the sheet: CE = in_4; CLK = in_2; CLR = in_3; LM = in_1; WM = in_5

  // Notes on the sheet:
  //   Random Access Memory (RAM)
  //   Random Access Memory (RAM)
endmodule
