// Logisim project SAP1.circ as structural Verilog: 7 circuits, main circuit main
module main (
  input  CLR,
  output [3:0] High,
  output [3:0] Low,
  output out_4,
  output out_5,
  output out_6,
  output out_7,
  output out_8,
  output out_9,
  output out_10,
  output out_11
);

  wire clock_1_out, control_sequencer_1_cp, control_sequencer_1_ea, control_sequencer_1_ep,
       control_sequencer_1_eu, control_sequencer_1_hlt, control_sequencer_1_nce, control_sequencer_1_nel,
       control_sequencer_1_nla, control_sequencer_1_nlb, control_sequencer_1_nll, control_sequencer_1_nlm,
       control_sequencer_1_nlo, control_sequencer_1_su, controlled_buffer_1_out, controlled_buffer_7_out,
       not_1_out, not_2_out, not_3_out, not_4_out, not_5_out, not_6_out, not_7_out, not_8_out, not_9_out;
  wire [3:0] Counter_q, MAR_q;
  wire [7:0] adder_1_out, controlled_buffer_6_out, Inst_Reg_q, Reg_A_q, Reg_B_q;

  Counter #(.width(4), .max(15), .trigger("falling")) Counter (
    .Q(Counter_q), .clk(controlled_buffer_1_out), .clr(CLR));  // open: load, D, count, carry
  assign controlled_buffer_1_out = control_sequencer_1_cp ? controlled_buffer_7_out : 1'bz;  // Controlled_Buffer controlled_buffer_1
  Register #(.width(4), .trigger("rising")) MAR (
    .D(Low), .en(not_1_out), .Q(MAR_q), .clk(controlled_buffer_7_out), .clr(CLR));
  not not_1 (not_1_out, control_sequencer_1_nlm);
  not not_2 (not_2_out, control_sequencer_1_nce);
  Register #(.width(8), .trigger("rising")) Inst_Reg (
    .D({High, Low}), .en(not_3_out), .Q(Inst_Reg_q), .clk(controlled_buffer_7_out), .clr(CLR));
  not not_3 (not_3_out, control_sequencer_1_nll);
  Control_Sequencer control_sequencer_1 (
    .CLK(controlled_buffer_7_out), .CLR(CLR), .Ep(control_sequencer_1_ep), .Cp(control_sequencer_1_cp),
    .l7(Inst_Reg_q[7]), .l6(Inst_Reg_q[6]), .l5(Inst_Reg_q[5]), .l4(Inst_Reg_q[4]),
    .HLT(control_sequencer_1_hlt), .nLm(control_sequencer_1_nlm), .nCE(control_sequencer_1_nce),
    .nEl(control_sequencer_1_nel), .nLa(control_sequencer_1_nla), .Ea(control_sequencer_1_ea),
    .Su(control_sequencer_1_su), .Eu(control_sequencer_1_eu), .nLb(control_sequencer_1_nlb),
    .nLo(control_sequencer_1_nlo), .nLl(control_sequencer_1_nll));
  assign Low = control_sequencer_1_ep ? Counter_q : 4'bz;  // Controlled_Buffer controlled_buffer_2
  RAM #(.addrWidth(4), .dataWidth(8), .bus("combined")) ram_1 (
    .addr(MAR_q), .data({High, Low}), .ld(not_2_out));  // open: sel, clk, clr
  not not_4 (not_4_out, control_sequencer_1_nel);
  assign Low = not_4_out ? Inst_Reg_q[3:0] : 4'bz;  // Controlled_Buffer controlled_buffer_3
  assign {High, Low} = control_sequencer_1_ea ? Reg_A_q : 8'bz;  // Controlled_Buffer controlled_buffer_4
  assign {High, Low} = control_sequencer_1_eu ? adder_1_out : 8'bz;  // Controlled_Buffer controlled_buffer_5
  not not_5 (not_5_out, control_sequencer_1_nla);
  Register #(.width(8), .trigger("rising")) Reg_A (
    .D({High, Low}), .en(not_5_out), .Q(Reg_A_q), .clk(controlled_buffer_7_out), .clr(CLR));
  Adder #(.width(8)) adder_1 (
    .a(Reg_A_q), .b(controlled_buffer_6_out), .out(adder_1_out), .cin(control_sequencer_1_su));  // open: cout
  assign controlled_buffer_6_out = not_8_out ? Reg_B_q : 8'bz;  // Controlled_Buffer controlled_buffer_6
  assign controlled_buffer_6_out = control_sequencer_1_su ? ~Reg_B_q : 8'bz;  // Controlled_Inverter controlled_inverter_1
  Register #(.width(8), .trigger("rising")) Reg_B (
    .D({High, Low}), .en(not_6_out), .Q(Reg_B_q), .clk(controlled_buffer_7_out), .clr(CLR));
  not not_6 (not_6_out, control_sequencer_1_nlb);
  Register #(.width(8), .trigger("rising")) Output (
    .D({High, Low}), .en(not_7_out), .Q({out_11, out_10, out_9, out_8, out_7, out_6, out_5, out_4}),
    .clk(controlled_buffer_7_out), .clr(CLR));
  not not_7 (not_7_out, control_sequencer_1_nlo);
  not not_8 (not_8_out, control_sequencer_1_su);
  Clock #(.highDuration(1), .lowDuration(1)) clock_1 (.out(clock_1_out));
  not not_9 (not_9_out, control_sequencer_1_hlt);
  assign controlled_buffer_7_out = not_9_out ? clock_1_out : 1'bz;  // Controlled_Buffer controlled_buffer_7
  Hex_Digit_Display hex_digit_display_1 (.value({out_7, out_6, out_5, out_4}));  // open: dp
  Hex_Digit_Display hex_digit_display_2 (.value({out_11, out_10, out_9, out_8}));  // open: dp

  // Notes on the sheet:
  //   Joshua Corbin
  //   SAP-1
  //   The Evergreen State College
  //   Controller
  //   ADD/SUB
  //   Mnemonic
  //   Load A
  //   Add A + B
  //   Subtract A - B
  //   Output
  //   Halt
  //   Program Currently in Ram
  //   5 + 11 - 6
  //   Mnemonic Commands
  //   Halt Program
  //   Assembly Language Commands
  //   Binary Op Code
  //   0000
  //   0001
  //   0010
  //   1110
  //   1111
  //   Load A from Memory Location 8 (value 05)
  //   Output Value in Register A to LEDs/HEX Display
  //   Add Memory Location 9 (value 11) to value in Register A (value 05)
  //   Subtract Memory Location 10 (value 6) from Register A (value 16)
endmodule

module Control_Sequencer (
  input  CLK,
  input  CLR,
  input  l7,
  input  l5,
  input  l6,
  input  l4,
  output Ep,
  output Cp,
  output HLT,
  output nLm,
  output nCE,
  output nEl,
  output nLa,
  output Ea,
  output Eu,
  output nLb,
  output nLl,
  output Su,
  output nLo
);

  wire c39_1_out_7, c39_1_out_8, c39_1_out_9, c39_1_out_10, c40_1_out_7, c40_1_out_8, c40_1_out_9,
       c40_1_out_10, c41_1_out_8, c41_1_out_9, c41_1_out_10, c41_1_out_11, c41_2_out_10, c41_2_out_11,
       c43_1_out_6, c43_1_out_7, c43_1_out_8, idecoder_1_add, idecoder_1_lda, idecoder_1_out, idecoder_1_sub,
       nor_1_out, not_1_out, or_1_out, or_2_out, or_3_out, or_4_out, or_6_out, shift_register_1_q2,
       shift_register_1_q3, shift_register_1_q4, shift_register_1_q5;

  iDecoder idecoder_1 (
    .l7(l7), .l6(l6), .l5(l5), .l4(l4), .LDA(idecoder_1_lda), .ADD(idecoder_1_add), .SUB(idecoder_1_sub),
    .OUT(idecoder_1_out), .HLT(HLT));
  C39 c39_1 (
    ._1(idecoder_1_lda), ._4(idecoder_1_add), ._9(idecoder_1_sub), ._10(shift_register_1_q3),
    ._12(idecoder_1_lda), ._13(shift_register_1_q4), .out_7(c39_1_out_7), .out_8(c39_1_out_8),
    .out_9(c39_1_out_9), .out_10(c39_1_out_10));
  not not_1 (not_1_out, CLK);
  C40 c40_1 (
    ._1(idecoder_1_add), ._4(idecoder_1_sub), ._5(shift_register_1_q4), ._9(idecoder_1_lda),
    ._12(idecoder_1_add), ._13(shift_register_1_q3), .out_7(c40_1_out_7), .out_8(c40_1_out_8),
    .out_9(c40_1_out_9), .out_10(c40_1_out_10));
  or or_1 (or_1_out, Ep, c39_1_out_7, c39_1_out_8, c39_1_out_9);
  or or_2 (or_2_out, shift_register_1_q2, c39_1_out_10, c40_1_out_7, c40_1_out_8);
  not not_2 (nLm, or_1_out);
  not not_3 (nCE, or_2_out);
  Shift_Register #(.width(1), .length(6), .parallel("true"), .trigger("rising")) shift_register_1 (
    .in(nor_1_out), .clk(not_1_out), .clr(CLR), .q0(Ep), .q1(Cp), .q2(shift_register_1_q2),
    .q3(shift_register_1_q3), .q4(shift_register_1_q4), .q5(shift_register_1_q5));  // open: shift, out, load, d0, d1, d2, d3, d4, d5
  C41 c41_1 (
    ._1(idecoder_1_sub), ._2(shift_register_1_q3), ._4(idecoder_1_lda), ._5(shift_register_1_q4),
    ._9(idecoder_1_add), ._12(idecoder_1_sub), ._13(shift_register_1_q5), .out_8(c41_1_out_8),
    .out_9(c41_1_out_9), .out_10(c41_1_out_10), .out_11(c41_1_out_11));
  or or_3 (or_3_out, c40_1_out_9, c40_1_out_10, c41_1_out_8);
  not not_4 (nEl, or_3_out);
  C41 c41_2 (
    ._1(idecoder_1_out), ._2(shift_register_1_q3), ._4(idecoder_1_sub), ._5(shift_register_1_q5),
    ._9(idecoder_1_add), ._12(idecoder_1_sub), ._13(shift_register_1_q5), .out_8(Ea), .out_9(Su),
    .out_10(c41_2_out_10), .out_11(c41_2_out_11));
  or or_4 (or_4_out, c41_1_out_9, c41_1_out_10, c41_1_out_11);
  not not_5 (nLa, or_4_out);
  C43 c43_1 (
    ._1(idecoder_1_add), ._4(idecoder_1_sub), ._5(shift_register_1_q4), ._9(idecoder_1_out),
    ._10(shift_register_1_q3), .out_6(c43_1_out_6), .out_7(c43_1_out_7), .out_8(c43_1_out_8));
  or or_5 (Eu, c41_2_out_10, c41_2_out_11);
  nor nor_1 (nor_1_out, Ep, Cp, shift_register_1_q2, shift_register_1_q3, shift_register_1_q4);
  or or_6 (or_6_out, c43_1_out_6, c43_1_out_7);
  not not_6 (nLo, c43_1_out_8);
  not not_7 (nLb, or_6_out);
  not not_8 (nLl, shift_register_1_q2);
endmodule

module C39 (
  input  _1,
  input  _4,
  input  _9,
  input  _10,
  input  _13,
  input  _12,
  output out_7,
  output out_8,
  output out_9,
  output out_10
);

  and and_1 (out_8, _4, _10);
  and and_2 (out_7, _1, _10);
  and and_3 (out_10, _12, _13);
  and and_4 (out_9, _9, _10);
endmodule

module C40 (
  input  _1,
  input  _4,
  input  _5,
  input  _9,
  input  _12,
  input  _13,
  output out_7,
  output out_8,
  output out_9,
  output out_10
);

  and and_1 (out_7, _1, _5);
  and and_2 (out_8, _4, _5);
  and and_3 (out_10, _12, _13);
  and and_4 (out_9, _9, _13);
endmodule

module C41 (
  input  _4,
  input  _5,
  input  _12,
  input  _13,
  input  _1,
  input  _2,
  input  _9,
  output out_8,
  output out_9,
  output out_10,
  output out_11
);

  and and_1 (out_9, _4, _5);
  and and_2 (out_8, _1, _2);
  and and_3 (out_10, _9, _13);
  and and_4 (out_11, _12, _13);
endmodule

module C43 (
  input  _1,
  input  _4,
  input  _5,
  input  _9,
  input  _10,
  output out_6,
  output out_7,
  output out_8
);

  and and_1 (out_6, _1, _5);
  and and_2 (out_7, _4, _5);
  and and_3 (out_8, _9, _10);
endmodule

module iDecoder (
  input  l7,
  input  l6,
  input  l5,
  input  l4,
  output LDA,
  output ADD,
  output SUB,
  output OUT,
  output HLT
);

  wire and_1_out, and_2_out, and_3_out, and_4_out, and_5_out, not_1_out, not_2_out, not_3_out, not_4_out;

  not not_1 (not_1_out, l7);
  not not_2 (not_2_out, l6);
  not not_3 (not_3_out, l5);
  not not_4 (not_4_out, l4);
  and and_1 (and_1_out, not_1_out, not_2_out, not_3_out, not_4_out);
  and and_2 (and_2_out, not_1_out, not_2_out, not_3_out, l4);
  and and_3 (and_3_out, not_1_out, not_2_out, l5, not_4_out);
  and and_4 (and_4_out, l7, l6, l5, not_4_out);
  and and_5 (and_5_out, l7, l6, l5, l4);
  buf buffer_1 (LDA, and_1_out);
  buf buffer_2 (ADD, and_2_out);
  buf buffer_3 (SUB, and_3_out);
  buf buffer_4 (OUT, and_4_out);
  buf buffer_5 (HLT, and_5_out);
endmodule
