// Logisim project adders.circ as structural Verilog: 12 circuits, main circuit main
module main (
  input  [1:0] in_1,
  input  [3:0] in_2,
  input  [3:0] in_3,
  input  in_4,
  input  in_5,
  input  [1:0] in_6,
  output [3:0] out_7
);

  wire [3:0] undriven;

  Hex_Digit_Display hex_digit_display_1 (.value(in_2));  // open: dp
  Hex_Digit_Display hex_digit_display_2 (.value(in_3));  // open: dp
  Hex_Digit_Display hex_digit_display_3 (.value(undriven), .dp(in_4));
  Decoder #(.select(2)) decoder_1 (
    .out0(out_7[0]), .out1(out_7[1]), .out2(out_7[2]), .out3(out_7[3]), .sel(in_6), .en(in_5));
endmodule

module equiv (
  input  X,
  input  Y,
  output Z
);

  wire and_1_out, and_2_out, not_1_out, not_2_out;

  not not_1 (not_1_out, X);
  not not_2 (not_2_out, Y);
  _4bitadder u_4bitadder_1 ();  // open: X, Y, Z, C
  and and_1 (and_1_out, not_1_out, not_2_out);
  and and_2 (and_2_out, X, Y);
  or or_1 (Z, and_1_out, and_2_out);
endmodule

module bitadder (
  input  X,
  input  Y,
  input  C_1,
  output C,
  output Z
);

  wire and_1_out, and_2_out, xor_1_out;

  xor xor_1 (xor_1_out, X, Y);
  and and_1 (and_1_out, X, Y);
  and and_2 (and_2_out, xor_1_out, C_1);
  xor xor_2 (Z, xor_1_out, C_1);
  or or_1 (C, and_2_out, and_1_out);
endmodule

module _4bitadder (
  input  [3:0] X,
  input  [3:0] Y,
  output [3:0] Z,
  output C
);

  wire bitadder_1_c, bitadder_2_c, bitadder_3_c;

  bitadder bitadder_1 (.X(X[0]), .Y(Y[0]), .C_1(1'b0), .C(bitadder_1_c), .Z(Z[0]));
  bitadder bitadder_2 (.X(X[1]), .Y(Y[1]), .C_1(bitadder_1_c), .C(bitadder_2_c), .Z(Z[1]));
  bitadder bitadder_3 (.X(X[2]), .Y(Y[2]), .C_1(bitadder_2_c), .C(bitadder_3_c), .Z(Z[2]));
  bitadder bitadder_4 (.X(X[3]), .Y(Y[3]), .C_1(bitadder_3_c), .C(C), .Z(Z[3]));
endmodule

module _2bit_compare (
  input  [1:0] X,
  input  [1:0] Y,
  output T
);

  wire and_1_out, and_2_out, and_3_out, not_1_out, not_2_out, or_1_out;

  not not_1 (not_1_out, Y[0]);
  not not_2 (not_2_out, Y[1]);
  and and_1 (and_1_out, X[1], not_2_out);
  and and_2 (and_2_out, X[0], not_1_out);
  or or_1 (or_1_out, X[1], not_2_out);
  and and_3 (and_3_out, and_2_out, or_1_out);
  or or_2 (T, and_1_out, and_3_out);
endmodule

module _4bit_twoscomp (
  input  [3:0] X,
  output [3:0] TwosCompX
);

  wire [3:0] not_1_out;

  _4bitadder u_4bitadder_1 (.X(not_1_out), .Y(4'b0001), .Z(TwosCompX));  // open: C
  assign not_1_out = ~X;  // NOT_Gate not_1, 4 bits wide
endmodule

module _4bitsubtract (
  input  [3:0] X,
  input  [3:0] Y,
  output [3:0] Z
);

  wire [3:0] n4bit_twoscomp_1_twoscompx;

  _4bit_twoscomp u_4bit_twoscomp_1 (.X(Y), .TwosCompX(n4bit_twoscomp_1_twoscompx));
  _4bitadder u_4bitadder_1 (.X(X), .Y(n4bit_twoscomp_1_twoscompx), .Z(Z));  // open: C
endmodule

module _3bitdecoder (
  input  [2:0] in_1,
  output [7:0] out_2
);

  wire [2:0] not_1_out;

  assign not_1_out = ~in_1;  // NOT_Gate not_1, 3 bits wide
  and and_1 (out_2[0], not_1_out[0], not_1_out[1], not_1_out[2]);
  and and_2 (out_2[1], not_1_out[2], not_1_out[1], in_1[0]);
  and and_3 (out_2[2], not_1_out[2], in_1[1], not_1_out[0]);
  and and_4 (out_2[3], not_1_out[2], in_1[1], in_1[0]);
  and and_5 (out_2[4], in_1[2], not_1_out[1], not_1_out[0]);
  and and_6 (out_2[5], in_1[2], not_1_out[1], in_1[0]);
  and and_7 (out_2[6], in_1[2], in_1[1], not_1_out[0]);
  and and_8 (out_2[7], in_1[2], in_1[1], in_1[0]);
endmodule

module Encoder_4bitALU (
  input  in_1,
  input  [3:0] X,
  input  [3:0] Y,
  input  [2:0] Op,
  output [3:0] Z
);

  wire [3:0] adder_1_out, divider_1_out, multiplexer_1_out, multiplier_1_out, negator_1_out, negator_2_out,
       subtractor_1_out;

  Adder #(.width(4)) adder_1 (.a(X), .b(Y), .out(adder_1_out));  // open: cin, cout
  Subtractor #(.width(4)) subtractor_1 (.a(X), .b(Y), .out(subtractor_1_out));  // open: bin, bout
  Multiplier #(.width(4)) multiplier_1 (.a(X), .b(Y), .out(multiplier_1_out));  // open: cin, cout
  Divider #(.width(4)) divider_1 (.a(X), .b(Y), .out(divider_1_out));  // open: upper, rem
  Negator #(.width(4)) negator_1 (.in(X), .out(negator_1_out));
  Negator #(.width(4)) negator_2 (.in(Y), .out(negator_2_out));
  Multiplexer #(.select(3), .width(4)) multiplexer_1 (
    .in0(adder_1_out), .in1(subtractor_1_out), .in2(multiplier_1_out), .in3(divider_1_out),
    .in4(negator_1_out), .in5(negator_2_out), .out(multiplexer_1_out), .sel(Op));  // open: in6, in7, en
  assign Z = in_1 ? multiplexer_1_out : 4'bz;  // Controlled_Buffer controlled_buffer_1
endmodule

module sr (
  input  R,
  input  S,
  output NotQ,
  output Q
);

  nor nor_1 (NotQ, R, Q);
  nor nor_2 (Q, NotQ, S);
endmodule

module SR_control (
  input  in_1,
  input  in_2,
  input  in_3,
  output out_4,
  output out_5
);

  wire nand_1_out, nand_2_out;

  nand nand_1 (nand_1_out, in_1, in_2);
  nand nand_2 (nand_2_out, in_2, in_3);
  nand nand_3 (out_4, nand_1_out, out_5);
  nand nand_4 (out_5, out_4, nand_2_out);
endmodule

module counter (
  input  CLK,
  input  RST,
  output [3:0] out_3
);

  wire [3:0] adder_1_out;

  Adder #(.width(4)) adder_1 (.a(out_3), .b(4'b0001), .out(adder_1_out));  // open: cin, cout
  Register #(.width(4)) register_1 (.D(adder_1_out), .Q(out_3), .clk(CLK), .clr(RST));  // open: en
endmodule
